// Logisim project G2.circ as structural Verilog: 3 circuits, main circuit main
module main (
);

  wire ALUSrc, and_1_out, Branch, Jump, MemRead, MemtoReg, MemWrite, mips_alu_1_p4, RegDst,
       registerfile_1_p6, RegWrite, Tick;
  wire [1:0] ALUOp;
  wire [3:0] alu_control_1_out_2, imm_ctrl_1_out_2, mips_alu_1_p3;
  wire [4:0] multiplexer_2_out, multiplexer_3_out;
  wire [5:0] Control_p1;
  wire [23:0] bit_extender_4_out;
  wire [25:0] undriven;
  wire [27:0] bit_extender_1_out, shifter_1_out;
  wire [31:0] adder_1_p3, adder_2_p4, adder_3_p3, bit_extender_2_out, bit_extender_3_out, mips_alu_1_p5,
       mips_ram_1_p6, multiplexer_1_out, multiplexer_4_out, multiplexer_5_out, multiplexer_7_out,
       multiplexer_8_out, multiplexer_9_out, PC_q, registerfile_1_p7, shifter_2_out, shifter_3_out;

  Clock clock_1 (.out(Tick));
  Register #(.width(32)) PC (.D(multiplexer_8_out), .Q(PC_q), .clk(Tick));  // open: en, clr
  // PLA Control: pin names not known; wires that end beside it: Control_p1
  // Adder adder_1: pin names not known; wires that end beside it: PC_q, 32'h4, adder_1_p3
  // Adder adder_2: pin names not known; wires that end beside it: PC_q, PC_q, 32'h8, adder_2_p4
  // MIPSProgramROM mipsprogramrom_1: pin names not known; wires that end beside it: Tick
  assign bit_extender_1_out = {{2{1'b0}}, undriven};  // Bit_Extender bit_extender_1
  Multiplexer #(.width(32), .enable("false")) multiplexer_1 (
    .in0(multiplexer_9_out), .in1(adder_2_p4), .out(multiplexer_1_out), .sel(Jump));
  Shifter #(.width(28)) shifter_1 (.in(bit_extender_1_out), .\dist (5'b00010), .out(shifter_1_out));
  assign bit_extender_2_out = {{6{1'b0}}, undriven};  // Bit_Extender bit_extender_2
  Shifter #(.width(32)) shifter_2 (.in(bit_extender_2_out), .\dist (5'b00010), .out(shifter_2_out));
  Multiplexer #(.width(5), .enable("false")) multiplexer_2 (
    .in0(multiplexer_3_out), .in1({5{1'b1}}), .out(multiplexer_2_out), .sel(Jump));
  Multiplexer #(.width(5), .enable("false")) multiplexer_3 (
    .in0(undriven[20:16]), .in1(undriven[15:11]), .out(multiplexer_3_out), .sel(RegDst));
  Multiplexer #(.width(32), .enable("false")) multiplexer_4 (
    .in0({shifter_1_out, adder_1_p3[31:28]}), .in1(shifter_2_out), .out(multiplexer_4_out), .sel(RegWrite));
  // RegisterFile registerfile_1: pin names not known; wires that end beside it: multiplexer_1_out, RegWrite, multiplexer_2_out, undriven[25:21], undriven[20:16], registerfile_1_p6, registerfile_1_p7
  assign bit_extender_3_out = {{16{undriven[15]}}, undriven[15:0]};  // Bit_Extender bit_extender_3
  Multiplexer #(.width(32), .enable("false")) multiplexer_5 (
    .in0(registerfile_1_p7), .in1(bit_extender_3_out), .out(multiplexer_5_out), .sel(ALUSrc));
  ALU_control alu_control_1 (.in_1({ALUOp, undriven[5:0]}), .out_2(alu_control_1_out_2));
  Shifter #(.width(32)) shifter_3 (.in(bit_extender_3_out), .\dist (5'b00010), .out(shifter_3_out));
  // MIPS_ALU mips_alu_1: pin names not known; wires that end beside it: registerfile_1_p6, multiplexer_5_out, mips_alu_1_p3, mips_alu_1_p4, mips_alu_1_p5
  Multiplexer #(.width(4), .enable("false")) multiplexer_6 (
    .in0(alu_control_1_out_2), .in1(imm_ctrl_1_out_2), .out(mips_alu_1_p3), .sel(alu_control_1_out_2[3]));
  // Adder adder_3: pin names not known; wires that end beside it: adder_1_p3, shifter_3_out, adder_3_p3
  Bit_Extender #(.in_width(32), .out_width(24)) bit_extender_4 (.in(mips_alu_1_p5), .out(bit_extender_4_out));
  Imm__Ctrl imm_ctrl_1 (.in_1(Control_p1[3:0]), .out_2(imm_ctrl_1_out_2));
  Multiplexer #(.width(32), .enable("false")) multiplexer_7 (
    .in0(adder_1_p3), .in1(adder_3_p3), .out(multiplexer_7_out), .sel(and_1_out));
  and and_1 (and_1_out, Branch, mips_alu_1_p4);
  Multiplexer #(.width(32), .enable("false")) multiplexer_8 (
    .in0(multiplexer_7_out), .in1(multiplexer_4_out), .out(multiplexer_8_out), .sel(Jump));
  // MIPS_RAM mips_ram_1: pin names not known; wires that end beside it: bit_extender_4_out, registerfile_1_p7, MemWrite, MemRead, Tick, mips_ram_1_p6
  Multiplexer #(.width(32), .enable("false")) multiplexer_9 (
    .in0(mips_alu_1_p5), .in1(mips_ram_1_p6), .out(multiplexer_9_out), .sel(MemtoReg));
endmodule

module ALU_control (
  input  [7:0] in_1,
  output [3:0] out_2
);

  // PLA pla_1: pin names not known; wires that end beside it: in_1, out_2
endmodule

module Imm__Ctrl (
  input  [3:0] in_1,
  output [3:0] out_2
);

  // PLA Imm__Ctrl: pin names not known; wires that end beside it: in_1, out_2
endmodule
